// Logisim project biblioteca.circ as structural Verilog
module contador8bits (
  input  CLR,
  input  CLK,
  input  E,
  output Q0,
  output Q1,
  output Q2,
  output Q3,
  output Q4,
  output Q5,
  output Q6,
  output Q7
);

  wire and_1_out, and_2_out, and_3_out, and_4_out, and_5_out, and_6_out;

  T_Flip_Flop #(.Pre_Clr_Positions("BELOW_ABOVE")) t_ff_1 (.clk(CLK), .T(E), .Q(Q0), .reset(CLR));  // open: Qn, preset
  T_Flip_Flop #(.Pre_Clr_Positions("BELOW_ABOVE")) t_ff_2 (.clk(CLK), .T(Q0), .Q(Q1), .reset(CLR));  // open: Qn, preset
  and and_1 (and_1_out, Q0, Q1);
  T_Flip_Flop #(.Pre_Clr_Positions("BELOW_ABOVE")) t_ff_3 (
    .clk(CLK), .T(and_1_out), .Q(Q2), .reset(CLR));  // open: Qn, preset
  and and_2 (and_2_out, and_1_out, Q2);
  T_Flip_Flop #(.Pre_Clr_Positions("BELOW_ABOVE")) t_ff_4 (
    .clk(CLK), .T(and_2_out), .Q(Q3), .reset(CLR));  // open: Qn, preset
  and and_3 (and_3_out, and_2_out, Q3);
  T_Flip_Flop #(.Pre_Clr_Positions("BELOW_ABOVE")) t_ff_5 (
    .clk(CLK), .T(and_3_out), .Q(Q4), .reset(CLR));  // open: Qn, preset
  and and_4 (and_4_out, and_3_out, Q4);
  T_Flip_Flop #(.Pre_Clr_Positions("BELOW_ABOVE")) t_ff_6 (
    .clk(CLK), .T(and_4_out), .Q(Q5), .reset(CLR));  // open: Qn, preset
  and and_5 (and_5_out, and_4_out, Q5);
  T_Flip_Flop #(.Pre_Clr_Positions("BELOW_ABOVE")) t_ff_7 (
    .clk(CLK), .T(and_5_out), .Q(Q6), .reset(CLR));  // open: Qn, preset
  and and_6 (and_6_out, and_5_out, Q6);
  T_Flip_Flop #(.Pre_Clr_Positions("BELOW_ABOVE")) t_ff_8 (
    .clk(CLK), .T(and_6_out), .Q(Q7), .reset(CLR));  // open: Qn, preset
endmodule

module registrador4bits (
  input  Eclock,
  input  D1,
  input  D2,
  input  D3,
  input  D4,
  output Q1,
  output Q2,
  output Q3,
  output Q4
);

  D_Flip_Flop d_ff_1 (.clk(Eclock), .D(D1), .Q(Q1));  // open: Qn, preset, reset
  D_Flip_Flop d_ff_2 (.clk(Eclock), .D(D2), .Q(Q2));  // open: Qn, preset, reset
  D_Flip_Flop d_ff_3 (.clk(Eclock), .D(D3), .Q(Q3));  // open: Qn, preset, reset
  D_Flip_Flop d_ff_4 (.clk(Eclock), .D(D4), .Q(Q4));  // open: Qn, preset, reset
endmodule
